# Fritzing sketch RaspberryPI2-LCD-Wiring-Diagram (saved by Fritzing 0.9.2b)
breadboards: 1

parts:
  LCD1 = LCD screen
  Raspberry_Pi1 = Raspberry Pi 2

nets:
  VSS: LCD1.VSS, LCD1.V0, LCD1.R/W, LCD1.LED-, Raspberry_Pi1.GND
  VDD: LCD1.VDD, LCD1.LED+, Raspberry_Pi1.5V
  N1: LCD1.RS, Raspberry_Pi1.GPIO26
  N2: LCD1.E, Raspberry_Pi1.GPIO19
  N3: LCD1.DB4, Raspberry_Pi1.GPIO13
  N4: LCD1.DB5, Raspberry_Pi1.GPIO6
  N5: LCD1.DB6, Raspberry_Pi1.GPIO5
  N6: LCD1.DB7, Raspberry_Pi1.GPIO11
